// Logisim project Ctl_Conditional.circ as structural Verilog: 2 circuits, main circuit Conditional
module Conditional (
  input  Enable,
  input  [15:0] Instruction,
  input  Z,
  input  C,
  input  N,
  input  V,
  output [10:0] Offset,
  output Verified
);

  wire verification_1_verified;

  assign Offset = Enable ? Instruction[10:0] : 11'bz;  // Controlled_Buffer controlled_buffer_1
  Pull_Resistor pull_resistor_1 (.node(Offset));
  Verification verification_1 (
    .cond(Instruction[11:8]), .z(Z), .c(C), .n(N), .v(V), .verified(verification_1_verified));
  and and_1 (Verified, Enable, verification_1_verified);
endmodule

module Verification (
  input  [3:0] cond,
  input  z,
  input  c,
  input  n,
  input  v,
  output verified
);

  wire and_1_out, and_2_out, and_3_out, and_4_out, and_5_out, and_6_out, and_7_out, and_8_out, and_9_out,
       and_10_out, and_11_out, and_12_out, and_13_out, and_14_out, and_15_out, and_16_out, and_17_out,
       and_18_out, and_19_out, and_20_out, not_1_out, not_2_out, not_3_out, not_4_out, not_5_out, not_6_out,
       not_7_out, not_8_out;

  not not_1 (not_1_out, cond[3]);
  not not_2 (not_2_out, cond[2]);
  not not_3 (not_3_out, cond[1]);
  not not_4 (not_4_out, cond[0]);
  not not_5 (not_5_out, z);
  not not_6 (not_6_out, c);
  not not_7 (not_7_out, n);
  not not_8 (not_8_out, v);
  and and_1 (and_1_out, not_1_out, not_2_out, not_3_out, not_4_out, z);
  and and_2 (and_2_out, not_1_out, not_2_out, not_3_out, cond[0], not_5_out);
  and and_3 (and_3_out, not_2_out, not_3_out, cond[0], not_5_out, not_6_out);
  and and_4 (and_4_out, not_1_out, not_2_out, cond[1], not_4_out, c);
  and and_5 (and_5_out, not_1_out, not_2_out, cond[1], cond[0], not_6_out);
  and and_6 (and_6_out, not_1_out, cond[2], not_3_out, not_4_out, n);
  and and_7 (and_7_out, cond[2], not_4_out, not_5_out, n, v);
  and and_8 (and_8_out, not_1_out, cond[2], not_3_out, cond[0], not_7_out);
  and and_9 (and_9_out, cond[2], not_3_out, cond[0], not_7_out, v);
  and and_10 (and_10_out, cond[2], cond[1], not_4_out, v);
  and and_11 (and_11_out, not_1_out, cond[2], cond[1], cond[0], not_8_out);
  and and_12 (and_12_out, cond[3], not_2_out, not_3_out, not_4_out, not_5_out, c);
  and and_13 (and_13_out, cond[3], not_3_out, cond[0], z);
  and and_14 (and_14_out, cond[3], cond[1], not_4_out, not_7_out, not_8_out);
  and and_15 (and_15_out, cond[3], cond[1], not_4_out, n, v);
  and and_16 (and_16_out, cond[3], not_2_out, cond[1], cond[0], not_7_out, v);
  and and_17 (and_17_out, cond[3], not_2_out, cond[1], cond[0], n, not_8_out);
  and and_18 (and_18_out, cond[3], cond[2], not_4_out, not_5_out, not_7_out, not_8_out);
  and and_19 (and_19_out, cond[3], cond[2], not_3_out, cond[0], n, not_8_out);
  and and_20 (and_20_out, cond[3], cond[2], cond[1], not_4_out);
  or or_1 (verified, and_1_out, and_2_out, and_3_out, and_4_out, and_5_out, and_6_out, and_7_out, and_8_out, and_9_out, and_10_out, and_11_out, and_12_out, and_13_out, and_14_out, and_15_out, and_16_out, and_17_out, and_18_out, and_19_out, and_20_out);
endmodule
