// Logisim project Ctl_Flags_APSR.circ as structural Verilog: 1 circuit, main circuit Flags_APSR
module Flags_APSR (
  input  [3:0] Update_Mask,
  input  [3:0] Flags_In,
  input  Clk,
  input  Rst,
  output [3:0] Flags_Out
);

  wire [3:0] register_1_q, register_2_q, register_3_q, register_4_q;

  Register #(.width(4)) register_1 (.D(Flags_In), .en(Update_Mask[0]), .clk(Clk), .Q(register_1_q), .clr(Rst));
  Register #(.width(4)) register_2 (.D(Flags_In), .en(Update_Mask[1]), .clk(Clk), .Q(register_2_q), .clr(Rst));
  Register #(.width(4)) register_3 (.D(Flags_In), .en(Update_Mask[2]), .clk(Clk), .Q(register_3_q), .clr(Rst));
  Register #(.width(4)) register_4 (.D(Flags_In), .en(Update_Mask[3]), .clk(Clk), .Q(register_4_q), .clr(Rst));
  BitSelector #(.width(4)) bitselector_1 (.in(register_1_q), .out(Flags_Out[0]), .sel(2'b00));
  BitSelector #(.width(4)) bitselector_2 (.in(register_2_q), .out(Flags_Out[1]), .sel(2'b01));
  BitSelector #(.width(4)) bitselector_3 (.in(register_3_q), .out(Flags_Out[2]), .sel(2'b10));
  BitSelector #(.width(4)) bitselector_4 (.in(register_4_q), .out(Flags_Out[3]), .sel(2'b11));
endmodule
