// Logisim project Ctl_Load_Store.circ as structural Verilog: 1 circuit, main circuit Load_Store
module Load_Store (
  input  Enable,
  input  [15:0] Instruction,
  input  [31:0] Stack_Pointer,
  input  Clk,
  input  Reset,
  output Store,
  output Load,
  output [2:0] Rmd,
  output [31:0] RAM_Addr,
  output PC_Hold
);

  wire and_1_out, bitselector_1_out, comparator_1_gt, comparator_1_lt, not_1_out;
  wire [2:0] bitselector_4_out;
  wire [7:0] bitselector_2_out, bitselector_3_out;
  wire [31:0] adder_1_out, bit_extender_1_out;

  BitSelector #(.width(16)) bitselector_1 (.in(Instruction), .out(bitselector_1_out), .sel(4'b1011));
  BitSelector #(.group(8), .width(16)) bitselector_2 (.in(Instruction), .out(bitselector_2_out), .sel(1'b1));
  BitSelector #(.group(8), .width(16)) bitselector_3 (.in(Instruction), .out(bitselector_3_out), .sel(1'b0));
  BitSelector #(.group(3)) bitselector_4 (.in(bitselector_2_out), .out(bitselector_4_out), .sel(2'b00));
  assign bit_extender_1_out = {{24{1'b0}}, bitselector_3_out};  // Bit_Extender bit_extender_1
  Comparator #(.width(1)) comparator_1 (
    .a(bitselector_1_out), .b(1'b0), .gt(comparator_1_gt), .lt(comparator_1_lt));  // open: eq
  and and_1 (and_1_out, comparator_1_gt, not_1_out);
  Adder #(.width(32)) adder_1 (.a(bit_extender_1_out), .b(Stack_Pointer), .out(adder_1_out));  // open: cin, cout
  not not_1 (not_1_out, PC_Hold);
  D_Flip_Flop d_ff_1 (.D(and_1_out), .clk(Clk), .Q(PC_Hold), .reset(Reset));  // open: Qn, preset
  Multiplexer #(.enable("false")) multiplexer_1 (.in0(1'b0), .in1(comparator_1_lt), .out(Store), .sel(Enable));
  Multiplexer #(.enable("false")) multiplexer_2 (.in0(1'b0), .in1(comparator_1_gt), .out(Load), .sel(Enable));
  Multiplexer #(.enable("false"), .width(3)) multiplexer_3 (
    .in0(3'b000), .in1(bitselector_4_out), .out(Rmd), .sel(Enable));
  Multiplexer #(.enable("false"), .width(32)) multiplexer_4 (
    .in0({32{1'b0}}), .in1(adder_1_out), .out(RAM_Addr), .sel(Enable));

  // Notes on the sheet:
  //   Instruction: pull=down
  //   Delay load and hold PC for 1 cycle for the RAM to send out requested data 
endmodule
