// Logisim project Ctl_Shift_Add_Sub_Mov.circ as structural Verilog: 3 circuits, main circuit Shift_Add_Sub_Mov
module Shift_Add_Sub_Mov (
  input  [15:0] Instruction,
  input  Enable,
  output [3:0] ALU_Opcode,
  output [3:0] Flags_Update_Mask,
  output [2:0] Rd,
  output [4:0] Imm5,
  output [31:0] Imm32,
  output Imm32_Enable,
  output [2:0] Rm,
  output [2:0] Rn,
  output Carry
);

  wire and_4_out, and_5_out, and_6_out, and_8_out, decoder_1_out0, decoder_1_out1, decoder_1_out2,
       decoder_1_out3, decoder_1_out4, decoder_1_out5, decoder_1_out6, decoder_1_out7, decoder_2_out0,
       decoder_2_out1, decoder_2_out2, decoder_2_out3, or_1_out, or_2_out, or_3_out, or_4_out, or_5_out,
       or_6_out, or_7_out;
  wire [3:0] bit_extender_2_out, flags_1_flags_update_mask, opcode_1_sortie;
  wire [7:0] or_10_out;
  wire [15:0] and_7_out, and_9_out, and_10_out, and_11_out, bit_extender_1_out, bit_extender_3_out,
       bit_extender_4_out, bit_extender_5_out, bit_extender_6_out, bit_extender_7_out, INST;
  wire [15:3] and_12_out;
  wire [31:0] bit_extender_8_out, bit_extender_9_out, multiplexer_1_out, negator_1_out;

  assign bit_extender_1_out = {{15{Enable}}, Enable};  // Bit_Extender bit_extender_1
  assign INST = Instruction & bit_extender_1_out;  // AND_Gate and_1, 16 bits wide
  Decoder #(.select(3)) decoder_1 (
    .out0(decoder_1_out0), .out1(decoder_1_out1), .out2(decoder_1_out2), .out3(decoder_1_out3),
    .out4(decoder_1_out4), .out5(decoder_1_out5), .out6(decoder_1_out6), .out7(decoder_1_out7),
    .sel(INST[13:11]));  // open: en
  Decoder #(.select(2)) decoder_2 (
    .out0(decoder_2_out0), .out1(decoder_2_out1), .out2(decoder_2_out2), .out3(decoder_2_out3),
    .sel(INST[10:9]));  // open: en
  opcode opcode_1 (.Entree(INST[13:9]), .Sortie(opcode_1_sortie));
  assign bit_extender_2_out = {{3{Enable}}, Enable};  // Bit_Extender bit_extender_2
  Flags flags_1 (.codop(INST[13:11]), .flags_update_mask(flags_1_flags_update_mask));
  assign ALU_Opcode = opcode_1_sortie & bit_extender_2_out;  // AND_Gate and_2, 4 bits wide
  assign Flags_Update_Mask = bit_extender_2_out & flags_1_flags_update_mask;  // AND_Gate and_3, 4 bits wide
  or or_1 (or_1_out, decoder_1_out0, decoder_1_out1, decoder_1_out2);
  or or_2 (or_2_out, decoder_1_out4, decoder_1_out5);
  or or_3 (or_3_out, decoder_1_out6, decoder_1_out7);
  or or_4 (or_4_out, decoder_2_out2, decoder_2_out3);
  assign bit_extender_3_out = {{15{or_1_out}}, or_1_out};  // Bit_Extender bit_extender_3
  assign bit_extender_4_out = {{15{or_2_out}}, or_2_out};  // Bit_Extender bit_extender_4
  assign bit_extender_5_out = {{15{or_3_out}}, or_3_out};  // Bit_Extender bit_extender_5
  and and_4 (and_4_out, decoder_1_out3, or_4_out);
  and and_5 (and_5_out, decoder_1_out3, or_5_out);
  or or_5 (or_5_out, decoder_2_out0, decoder_2_out1);
  and and_6 (and_6_out, decoder_1_out3, or_6_out);
  or or_6 (or_6_out, decoder_2_out2, decoder_2_out3);
  or or_7 (or_7_out, decoder_2_out3, decoder_2_out1);
  assign {and_7_out[15:11], Imm5, and_7_out[5:0]} = bit_extender_3_out & INST;  // AND_Gate and_7, 16 bits wide
  and and_8 (and_8_out, or_7_out, decoder_1_out3);
  assign and_9_out = bit_extender_4_out & INST;  // AND_Gate and_9, 16 bits wide
  assign and_10_out = bit_extender_5_out & INST;  // AND_Gate and_10, 16 bits wide
  or or_8 (Imm32_Enable, and_4_out, decoder_1_out4, decoder_1_out5, decoder_1_out6, decoder_1_out7);
  assign bit_extender_6_out = {{15{and_5_out}}, and_5_out};  // Bit_Extender bit_extender_6
  assign bit_extender_7_out = {{15{and_6_out}}, and_6_out};  // Bit_Extender bit_extender_7
  or or_9 (Carry, and_8_out, decoder_1_out7);
  assign and_11_out = bit_extender_6_out & INST;  // AND_Gate and_11, 16 bits wide
  assign {and_12_out, and_12_out[8:6]} = bit_extender_7_out & INST;  // AND_Gate and_12, 16 bits wide
  assign or_10_out = and_9_out[7:0] | and_10_out[7:0];  // OR_Gate or_10, 8 bits wide
  assign Rd = and_7_out[2:0] | and_11_out[2:0] | and_12_out[8:6] | and_9_out[10:8] | and_10_out[10:8];  // OR_Gate or_11, 3 bits wide
  assign bit_extender_8_out = {{24{1'b0}}, or_10_out};  // Bit_Extender bit_extender_8
  assign Rn = and_11_out[5:3] | and_12_out[5:3] | and_7_out[5:3] | and_10_out[10:8];  // OR_Gate or_12, 3 bits wide
  assign bit_extender_9_out = {{29{1'b0}}, and_12_out[8:6]};  // Bit_Extender bit_extender_9
  Multiplexer #(.enable("false"), .width(32)) multiplexer_1 (
    .in0(bit_extender_8_out), .in1(negator_1_out), .out(multiplexer_1_out), .sel(decoder_1_out4));
  Negator #(.width(32)) negator_1 (.in(bit_extender_8_out), .out(negator_1_out));
  assign Imm32 = bit_extender_9_out | multiplexer_1_out;  // OR_Gate or_13, 32 bits wide
  assign Rm = and_7_out[5:3] | and_11_out[8:6];  // OR_Gate or_14, 3 bits wide

  // Notes on the sheet:
  //   Pull output low on Enable = 0
  //   ALU will use Imm32 instead of Rm
  //   Enable carry for SUB since it is reversed in ALU
  //   only ADD and SUB use Rm
endmodule

module Flags (
  input  [2:0] codop,
  output [3:0] flags_update_mask
);

  wire and_1_out, and_2_out, and_3_out, not_1_out;

  not not_1 (not_1_out, codop[2]);
  or or_1 (flags_update_mask[1], not_1_out, codop[0], codop[1]);
  and and_1 (and_1_out, codop[1], codop[0]);
  and and_2 (and_2_out, codop[2], codop[0]);
  and and_3 (and_3_out, codop[2], codop[1]);
  or or_2 (flags_update_mask[0], and_1_out, and_2_out, and_3_out);

  assign flags_update_mask[3:2] = 2'b11;
endmodule

module opcode (
  input  [4:0] Entree,
  output [3:0] Sortie
);

  wire and_2_out, and_3_out, and_4_out, and_5_out, and_6_out, and_7_out, not_1_out, not_2_out, not_3_out,
       not_4_out;

  not not_1 (not_1_out, Entree[4]);
  not not_2 (not_2_out, Entree[3]);
  not not_3 (not_3_out, Entree[2]);
  not not_4 (not_4_out, Entree[0]);
  and and_1 (Sortie[3], Entree[4], not_2_out);
  and and_2 (and_2_out, not_1_out, not_2_out);
  and and_3 (and_3_out, Entree[2], Entree[0]);
  and and_4 (and_4_out, Entree[4], Entree[2]);
  and and_5 (and_5_out, not_1_out, not_2_out, Entree[2]);
  and and_6 (and_6_out, not_1_out, Entree[2], not_4_out);
  and and_7 (and_7_out, Entree[4], not_3_out);
  or or_1 (Sortie[1], and_2_out, and_3_out, and_4_out);
  or or_2 (Sortie[0], and_5_out, and_6_out, and_7_out);

  assign Sortie[2] = Entree[3];
endmodule
